# Fritzing sketch esp01_primeros_pasos (saved by Fritzing 0.9.3b)
breadboards: 1

parts:
  U1 = ESP8266 WiFi Module [part_number=ESP8266]
  R1 = Resistor [tolerance=±5% resistance=470 package=THT]
  Componente1 = Arduino Uno (Rev3)
  R2 = Resistor [tolerance=±5% resistance=470 package=THT]
  R3 = Resistor [tolerance=±5% resistance=470 package=THT]
  R4 = Resistor [tolerance=±5% resistance=470 package=THT]

nets:
  N1: U1.RXD, R2.Pin_1
  VCC: U1.VCC, Componente1.3V3
  GND: U1.GND, R1.Pin_1, Componente1.GND, R4.Pin_0
  N2: U1.TXD, Componente1.D3_PWM
  N3: Componente1.D2, R2.Pin_0, R3.Pin_1
  N4: R3.Pin_0, R4.Pin_1

custom parts:
  ESP8266 WiFi Module: Generic WiFi Module based on the ESP8266 with onboard PCB antenna and UART communications
